# Fritzing sketch Dino (saved by Fritzing 0.9.3b)

parts:
  ARDUINO = Arduino Pro Mini v13
  LED1 = LED - 5mm [color="Red (633nm)" package="5 mm [THT]"]
  LED2 = LED - 5mm [color="Red (633nm)" package="5 mm [THT]"]
  R1 = Resistor [tolerance=±5% resistance=220 package=THT]

nets:
  N1: ARDUINO.D3_PWM, LED1.anode
  N2: ARDUINO.D2, LED2.anode
  N3: ARDUINO.GND, R1.Pin_1
  N4: LED1.cathode, LED2.cathode, R1.Pin_0
